// Logisim project Счетчик_на_D_триггерах.circ as structural Verilog: 1 circuit, main circuit main
module main (
  output out_1,
  output out_2,
  output out_3,
  output out_4,
  output out_5
);

  wire button_1_out, clock_1_out, nand_1_out, nand_2_out, nand_3_out, nand_4_out, nand_5_out, nand_6_out,
       nand_7_out, nand_8_out, nand_9_out, nand_10_out, nand_11_out, nand_12_out, nand_13_out, nand_14_out,
       nand_16_out, nand_17_out, nand_18_out, nand_19_out, nand_20_out, Q0_t_1, Q1_t_1, Q2_t_1, Q3_t_1,
       Q4_t_1;

  nand nand_1 (nand_1_out, out_1, out_1);
  nand nand_2 (nand_2_out, ~out_4, ~out_3, ~out_2);  // NAND_Gate
  nand nand_3 (nand_3_out, out_4, out_3, out_2);
  nand nand_4 (nand_4_out, out_5, out_3, out_2);
  nand nand_5 (nand_5_out, out_4, out_1);
  nand nand_6 (nand_6_out, out_4, ~out_3, out_2);  // NAND_Gate
  nand nand_7 (nand_7_out, out_5, ~out_4, ~out_3);  // NAND_Gate
  nand nand_8 (nand_8_out, ~out_5, ~out_4);  // NAND_Gate
  nand nand_9 (nand_9_out, out_5, out_4, out_3);
  nand nand_10 (nand_10_out, out_5, out_4, out_2);
  nand nand_11 (nand_11_out, ~out_5, out_2);  // NAND_Gate
  nand nand_12 (nand_12_out, ~out_5, out_4, out_3);  // NAND_Gate
  nand nand_13 (nand_13_out, ~out_5, out_1);  // NAND_Gate
  nand nand_14 (nand_14_out, out_4, ~out_3, ~out_2, ~out_1);  // NAND_Gate
  nand nand_15 (Q4_t_1, nand_14_out, nand_16_out);
  nand nand_16 (nand_16_out, ~out_5, ~out_4, out_3, ~out_2);  // NAND_Gate
  nand nand_17 (nand_17_out, ~out_4, ~out_3, ~out_2, ~out_1);  // NAND_Gate
  nand nand_18 (nand_18_out, ~out_5, ~out_4, out_3, out_2);  // NAND_Gate
  nand nand_19 (nand_19_out, ~out_4, ~out_3, ~out_2, ~out_1);  // NAND_Gate
  nand nand_20 (nand_20_out, out_5, ~out_3, ~out_2, ~out_1);  // NAND_Gate
  nand nand_21 (Q3_t_1, nand_1_out, nand_2_out, nand_3_out, nand_4_out);
  nand nand_22 (Q2_t_1, nand_5_out, nand_6_out, nand_7_out, nand_17_out, nand_18_out);
  nand nand_23 (Q1_t_1, nand_8_out, nand_9_out, nand_10_out, nand_19_out);
  nand nand_24 (Q0_t_1, nand_11_out, nand_12_out, nand_13_out, nand_20_out);
  Clock clock_1 (.out(clock_1_out));
  Button button_1 (.out(button_1_out));
  D_Flip_Flop d_ff_1 (.clk(clock_1_out), .D(Q4_t_1), .Q(out_1), .en(1'b1), .reset(button_1_out));  // open: Qn, preset
  D_Flip_Flop d_ff_2 (.clk(clock_1_out), .D(Q3_t_1), .Q(out_2), .en(1'b1), .reset(button_1_out));  // open: Qn, preset
  D_Flip_Flop d_ff_3 (.clk(clock_1_out), .D(Q2_t_1), .Q(out_3), .en(1'b1), .reset(button_1_out));  // open: Qn, preset
  D_Flip_Flop d_ff_4 (.clk(clock_1_out), .D(Q1_t_1), .Q(out_4), .en(1'b1), .reset(button_1_out));  // open: Qn, preset
  D_Flip_Flop d_ff_5 (.clk(clock_1_out), .D(Q0_t_1), .Q(out_5), .en(1'b1), .reset(button_1_out));  // open: Qn, preset
  Hex_Digit_Display hex_digit_display_1 (.value({out_2, out_3, out_4, out_5}));  // open: dp
  Hex_Digit_Display hex_digit_display_2 (.value({3'b000, out_1}));  // open: dp
  // Probe on {out_1, out_2, out_3, out_4, out_5}

  // Other names for the same wires on the sheet: Q0t = out_5; Q1t = out_4; Q2t = out_3; Q3t = out_2; Q4t = out_1
endmodule
