// Logisim project Счетчик_на_JK_триггерах.circ as structural Verilog: 1 circuit, main circuit main
module main (
  output out_1,
  output out_2,
  output out_3,
  output out_4,
  output out_5
);

  wire button_1_out, clock_1_out, nor_1_out, nor_2_out, nor_3_out, nor_4_out, nor_6_out, nor_8_out,
       nor_9_out, nor_11_out, nor_12_out, nor_14_out, nor_15_out, nor_16_out, nor_18_out, nor_19_out,
       nor_21_out, nor_22_out, nor_24_out, nor_25_out, Q0_t_1_J, Q0_t_1_K, Q1_t_1_J, Q1_t_1_K, Q2_t_1_J,
       Q2_t_1_K, Q3_t_1_J, Q3_t_1_K, Q4_t_1_J;

  nor nor_1 (nor_1_out, out_4, out_3);
  nor nor_2 (nor_2_out, ~out_4, ~out_3);  // NOR_Gate
  nor nor_3 (nor_3_out, ~out_5, ~out_3);  // NOR_Gate
  nor nor_4 (nor_4_out, ~out_4, out_1);  // NOR_Gate
  nor nor_5 (Q3_t_1_J, nor_4_out, out_3);
  nor nor_6 (nor_6_out, ~out_4, ~out_3);  // NOR_Gate
  nor nor_7 (Q3_t_1_K, nor_6_out, nor_8_out);
  nor nor_8 (nor_8_out, ~out_5, ~out_3);  // NOR_Gate
  nor nor_9 (nor_9_out, ~out_4, out_2, out_1);  // NOR_Gate
  nor nor_10 (Q2_t_1_J, nor_9_out, nor_11_out, nor_12_out);
  nor nor_11 (nor_11_out, out_5, out_4, ~out_2);  // NOR_Gate
  nor nor_12 (nor_12_out, out_5, out_4, ~out_1);  // NOR_Gate
  nor nor_13 (Q2_t_1_K, nor_14_out, nor_14_out);
  nor nor_14 (nor_14_out, out_5, out_4, ~out_2);  // NOR_Gate
  nor nor_15 (nor_15_out, ~out_5, ~out_3);  // NOR_Gate
  nor nor_16 (nor_16_out, ~out_5, ~out_2);  // NOR_Gate
  nor nor_17 (Q1_t_1_J, nor_15_out, nor_16_out, nor_18_out);
  nor nor_18 (nor_18_out, ~out_5, ~out_1);  // NOR_Gate
  nor nor_19 (nor_19_out, ~out_5, ~out_3);  // NOR_Gate
  nor nor_20 (Q1_t_1_K, nor_19_out, nor_21_out);
  nor nor_21 (nor_21_out, ~out_5, ~out_2);  // NOR_Gate
  nor nor_22 (nor_22_out, out_3, out_2, out_1);
  nor nor_23 (Q0_t_1_J, nor_22_out, nor_24_out);
  nor nor_24 (nor_24_out, out_4, ~out_3, out_2);  // NOR_Gate
  nor nor_25 (nor_25_out, out_3, out_2, out_1);
  nor nor_26 (Q0_t_1_K, nor_25_out, nor_25_out);
  nor nor_27 (Q4_t_1_J, nor_1_out, out_2, nor_2_out, nor_3_out);
  Clock clock_1 (.out(clock_1_out));
  Button button_1 (.out(button_1_out));
  J_K_Flip_Flop j_k_ff_1 (
    .J(Q4_t_1_J), .clk(clock_1_out), .K(1'b1), .Q(out_1), .en(1'b1), .reset(button_1_out));  // open: Qn, preset
  J_K_Flip_Flop j_k_ff_2 (
    .J(Q3_t_1_J), .clk(clock_1_out), .K(Q3_t_1_K), .Q(out_2), .en(1'b1), .reset(button_1_out));  // open: Qn, preset
  J_K_Flip_Flop j_k_ff_3 (
    .J(Q2_t_1_J), .clk(clock_1_out), .K(Q2_t_1_K), .Q(out_3), .en(1'b1), .reset(button_1_out));  // open: Qn, preset
  J_K_Flip_Flop j_k_ff_4 (
    .J(Q1_t_1_J), .clk(clock_1_out), .K(Q1_t_1_K), .Q(out_4), .en(1'b1), .reset(button_1_out));  // open: Qn, preset
  J_K_Flip_Flop j_k_ff_5 (
    .J(Q0_t_1_J), .clk(clock_1_out), .K(Q0_t_1_K), .Q(out_5), .en(1'b1), .reset(button_1_out));  // open: Qn, preset
  Hex_Digit_Display hex_digit_display_1 (.value({3'b000, out_1}));  // open: dp
  Hex_Digit_Display hex_digit_display_2 (.value({out_2, out_3, out_4, out_5}));  // open: dp
  // Probe on {out_1, out_2, out_3, out_4, out_5}

  // Other names for the same wires on the sheet: Q0t = out_5; Q1t = out_4; Q2t = out_3; Q3t = out_2; Q4t = out_1
endmodule
