// Logisim project защита.circ as structural Verilog: 1 circuit, main circuit main
module main (
);

  wire clock_1_out;
  wire [4:0] register_1_q, rom_1_data;

  ROM #(.addrWidth(5), .dataWidth(5)) rom_1 (.addr(register_1_q), .data(rom_1_data));  // open: sel
  Clock clock_1 (.out(clock_1_out));
  // Probe on register_1_q
  Register #(.width(5)) register_1 (.D(rom_1_data), .Q(register_1_q), .clk(clock_1_out));  // open: en, clr

  // Notes on the sheet:
  //   contents of rom_1 (hex, n*v repeats v):
  //   e f 10 11 12 0 1 2 3 4 5 6 7 8 9 a b c d
endmodule
