// Logisim project Задание №1.circ as structural Verilog: 1 circuit, main circuit main
module main (
  input  T,
  output L,
  output out_3
);

  wire and_1_out, and_2_out, and_3_out, and_4_out, and_5_out, and_6_out, and_7_out, and_8_out, and_9_out,
       and_10_out, button_1_out, clock_1_out, d_ff_1_q, d_ff_2_q, or_1_out, or_2_out;
  wire [1:0] register_1_q, rom_1_data;

  and and_1 (and_1_out, ~d_ff_1_q, ~d_ff_2_q, T);  // AND_Gate
  and and_2 (and_2_out, d_ff_1_q, ~d_ff_2_q, ~T);  // AND_Gate
  and and_3 (and_3_out, d_ff_1_q, ~d_ff_2_q, T);  // AND_Gate
  and and_4 (and_4_out, d_ff_1_q, d_ff_2_q, T);
  and and_5 (and_5_out, ~d_ff_1_q, ~d_ff_2_q, ~T);  // AND_Gate
  and and_6 (and_6_out, ~d_ff_1_q, d_ff_2_q, ~T);  // AND_Gate
  and and_7 (and_7_out, d_ff_1_q, ~d_ff_2_q, ~T);  // AND_Gate
  and and_8 (and_8_out, d_ff_1_q, d_ff_2_q, ~T);  // AND_Gate
  Clock clock_1 (.out(clock_1_out));
  or or_1 (or_1_out, and_1_out, and_2_out, and_3_out, and_4_out);
  or or_2 (or_2_out, and_5_out, and_6_out, and_7_out, and_8_out);
  ROM #(.addrWidth(3), .dataWidth(2)) rom_1 (.addr({register_1_q, T}), .data(rom_1_data));  // open: sel
  Button button_1 (.out(button_1_out));
  D_Flip_Flop d_ff_1 (
    .clk(clock_1_out), .D(or_1_out), .Q(d_ff_1_q), .en(1'b1), .reset(button_1_out));  // open: Qn, preset
  D_Flip_Flop d_ff_2 (
    .clk(clock_1_out), .D(or_2_out), .Q(d_ff_2_q), .en(1'b1), .reset(button_1_out));  // open: Qn, preset
  Register #(.width(2)) register_1 (.D(rom_1_data), .Q(register_1_q), .clk(clock_1_out));  // open: en, clr
  and and_9 (and_9_out, d_ff_1_q, ~d_ff_2_q);  // AND_Gate
  and and_10 (and_10_out, d_ff_1_q, d_ff_2_q);
  ROM #(.addrWidth(2), .dataWidth(1)) rom_2 (.addr(register_1_q), .data(out_3));  // open: sel
  or or_3 (L, and_9_out, and_10_out);

  // Notes on the sheet:
  //   S1
  //   S0
  //   contents of rom_1 (hex, n*v repeats v):
  //   1 2 1 0 3 2 1 2
  //   S1
  //   S0
  //   contents of rom_2 (hex, n*v repeats v):
  //   0 0 1 1
endmodule
