// Logisim project Задание №2.circ as structural Verilog: 3 circuits, main circuit main
module main (
  input  IN1,
  input  IN2,
  output out_3
);

  wire clk, \автомат1_1_out , \автомат1_2_out , \автомат_1_out , \автомат_2_out ;

  Clock clock_1 (.out(clk));
  \Автомат  \u_автомат_1  (.OUT(\автомат_1_out ), .IN1(IN1), .IN2(IN2), .clk(clk));
  \Автомат  \u_автомат_2  (.OUT(\автомат_2_out ), .IN1(IN2), .IN2(IN1), .clk(clk));
  \Автомат1  \u_автомат1_1  (.clk(clk), .OUT(\автомат1_1_out ), .In(IN1), .q(\автомат_1_out ));
  \Автомат1  \u_автомат1_2  (.clk(clk), .OUT(\автомат1_2_out ), .In(IN2), .q(\автомат_2_out ));
  or or_1 (out_3, \автомат1_1_out , \автомат1_2_out );

  // Notes on the sheet:
  //   clk
endmodule

module \Автомат  (
  input  IN1,
  input  IN2,
  input  clk,
  output OUT
);

  wire [2:0] rom_1_data;
  wire [4:2] register_1_q;

  ROM #(.addrWidth(5), .dataWidth(3)) rom_1 (.addr({register_1_q, IN1, IN2}), .data(rom_1_data));  // open: sel
  Register #(.width(3)) register_1 (.D(rom_1_data), .Q(register_1_q), .clk(clk));  // open: en, clr
  ROM #(.addrWidth(5), .dataWidth(1)) rom_2 (.addr({register_1_q, IN1, IN2}), .data(OUT));  // open: sel

  // Notes on the sheet:
  //   contents of rom_1 (hex, n*v repeats v):
  //   1 0 2 0 1 0 0 3 0 0 2 4 1 0 2 3 1 0 2 4
  //   contents of rom_2 (hex, n*v repeats v):
  //   12*0 1 0 1 0 1 0 1
endmodule

module \Автомат1  (
  input  In,
  input  q,
  input  clk,
  output OUT
);

  wire rom_2_data;
  wire [1:0] register_1_q, rom_1_data;

  ROM #(.addrWidth(4), .dataWidth(2)) rom_1 (.addr({register_1_q, In, q}), .data(rom_1_data));  // open: sel
  Register #(.width(2)) register_1 (.D(rom_1_data), .Q(register_1_q), .clk(clk));  // open: en, clr
  ROM #(.addrWidth(4), .dataWidth(1)) rom_2 (.addr({register_1_q, In, q}), .data(rom_2_data));  // open: sel
  D_Flip_Flop d_ff_1 (.clk(clk), .D(rom_2_data), .Q(OUT));  // open: Qn, preset, en, reset

  // Notes on the sheet:
  //   contents of rom_1 (hex, n*v repeats v):
  //   0 0 1 0 0 0 1 2 0 0 2 2
  //   contents of rom_2 (hex, n*v repeats v):
  //   5*0 1 0 0 1 1
endmodule
