// Logisim project Задание №3.circ as structural Verilog: 2 circuits, main circuit main
module main (
  input  in_1,
  input  in_2,
  output out_3
);

  wire clock_1_out, \автомат_1_out_4 , \автомат_2_out_4 ;

  Clock clock_1 (.out(clock_1_out));
  \Автомат  \u_автомат_1  (.d(in_1), .m(out_3), .in_3(clock_1_out), .out_4(\автомат_1_out_4 ));
  \Автомат  \u_автомат_2  (.d(in_2), .m(out_3), .in_3(clock_1_out), .out_4(\автомат_2_out_4 ));
  and and_1 (out_3, \автомат_1_out_4 , \автомат_2_out_4 );
endmodule

module \Автомат  (
  input  d,
  input  m,
  input  in_3,
  output out_4
);

  wire and_1_out, d_ff_1_q, or_1_out;

  and and_1 (and_1_out, d, ~m);  // AND_Gate
  or or_1 (or_1_out, d_ff_1_q, and_1_out);
  D_Flip_Flop d_ff_1 (.clk(in_3), .D(or_1_out), .Q(d_ff_1_q));  // open: Qn, preset, en, reset
  or or_2 (out_4, d, d_ff_1_q);
endmodule
