// Logisim project Вычислительное Устройство_Две Операции ДУ.circ as structural Verilog: 3 circuits, main circuit main
module main (
  input  [7:0] in_1,
  input  [15:0] in_2,
  input  in_3,
  output [15:0] out_4,
  output [8:0] out_5,
  output [8:0] out_6
);

  wire ceo, clk, P0, P1, P2, P3, P4, RI_out, rst, \оа_1_error , \оа_1_error_2 ;
  wire [26:0] Y;

  Clock clock_1 (.out(clk));
  Button RI (.out(RI_out));
  Button button_1 (.out(rst));
  filter filter_1 (.in_1(clk), .in_2(RI_out), .in_3(1'b1), .out_5(ceo));  // open: out_4
  // Probe on in_1
  // Probe on out_5
  // Probe on out_6
  \ОА  \u_оа_1  (
    .OMinput(in_3), .\input (clk), .in_3(in_1), .in_4(in_2), .in_5(Y), .P0(P0), .P1(P1), .P2(P2),
    .ERROR(\оа_1_error ), .out_10(out_6), .out_11(out_5), .P3(P3), .ERROR_2(\оа_1_error_2 ), .out_14(out_4),
    .P4(P4));
  LED led_1 (.in(\оа_1_error ));
  LED led_2 (.in(\оа_1_error_2 ));
  \УА  \u_уа_1  (.RI(ceo), .P0(P0), .P1(P1), .P2(P2), .P3(P3), .P4(P4), .Ready_RST(rst), .out_9(Y), .clk(clk));

  // Notes on the sheet:
  //   Ready RST
  //   Результат выполнения умножения чисел, представленных в IEEE754
  //   Ввод для деления
  //   Ввод для умножения
  //   Значение частного
  //   Значение остатка
endmodule

module \УА  (
  input  RI,
  input  P0,
  input  P1,
  input  P2,
  input  P3,
  input  P4,
  input  Ready_RST,
  input  clk,
  output [26:0] out_9
);

  wire multiplexer_1_out;
  wire [2:0] rom_3_data;
  wire [4:0] multiplexer_2_out, register_1_q, rom_1_data, rom_2_data;

  Multiplexer #(.select(3), .disabled(0), .enable("false")) multiplexer_1 (
    .in0(RI), .in1(P0), .in2(P1), .in3(P2), .in4(P3), .in5(P4), .in6(Ready_RST), .out(multiplexer_1_out),
    .sel(rom_3_data));  // open: in7
  Multiplexer #(.width(5), .disabled(0), .enable("false")) multiplexer_2 (
    .in0(rom_1_data), .in1(rom_2_data), .out(multiplexer_2_out), .sel(multiplexer_1_out));
  Register #(.width(5)) register_1 (.D(multiplexer_2_out), .Q(register_1_q), .clk(clk));  // open: en, clr
  ROM #(.addrWidth(5), .dataWidth(5)) rom_1 (.addr(register_1_q), .data(rom_1_data));  // open: sel
  ROM #(.addrWidth(5), .dataWidth(5)) rom_2 (.addr(register_1_q), .data(rom_2_data));  // open: sel
  ROM #(.addrWidth(5), .dataWidth(3)) rom_3 (.addr(register_1_q), .data(rom_3_data));  // open: sel
  ROM #(.addrWidth(5), .dataWidth(27)) rom_4 (.addr(register_1_q), .data(out_9));  // open: sel

  // Notes on the sheet:
  //   contents of rom_1 (hex, n*v repeats v):
  //   18 19 1a 4 5 6 8 1d 9 a b c 9 1d 1c 11 1d 12 13 14 15 14 17 1d 18 19 1a 1b 1c 1d
  //   contents of rom_2 (hex, n*v repeats v):
  //   1 1b 3 4 5 6 7 0 9 a b c d 0 f 10 0 12 13 14 15 16 17 0 1 2 3 e f
  //   contents of rom_3 (hex, n*v repeats v):
  //   0 1 4*0 2 6 4*0 3 6 0 4 6 4*0 5 0 6 5*0 6
  //   contents of rom_4 (hex, n*v repeats v):
  //   1 4000000 2000000 1000000 c00000 200000 100000 80000 40000 28000 2000 10000 1000 800 400 200 100 80
  //   40 20 10 8 6 6*0 800
  //   ЗАДАННЫХ В ФОРМАТЕ IEEE754
  //   УПРАВЛЯЮЩИЙ АВТОМАТ ВЫЧИСЛИТЕЛЬНОГО УСТРОЙСТВА,
  //   ВЫПОЛНЯЮЩЕГО ОПЕРАЦИЮ ДЕЛЕНИЯ ЧИСЕЛ, ЗАДАННЫХ
  //   В ДОПОЛНИТЕЛЬНОМ КОДЕ И ОПЕРАЦИЮ УМНОЖЕНИЯ ЧИСЕЛ,
endmodule

module \ОА  (
  input  OMinput,
  input  \input ,
  input  [7:0] in_3,
  input  [15:0] in_4,
  input  [26:0] in_5,
  output P0,
  output P1,
  output P2,
  output ERROR,
  output [8:0] out_10,
  output [8:0] out_11,
  output P3,
  output ERROR_2,
  output [15:0] out_14,
  output P4
);

  wire not_1_out, not_3_out, OperatingMode, out_sign_A, out_sign_B, QSA, QSB, signA, signB, signS, xor_1_out;
  wire [3:0] counter_1_q;
  wire [6:0] RG_Sexp;
  wire [7:0] ABS_A, ABS_B, not_2_out, NOT_B, output_A, output_B;
  wire [8:0] RG_E, RG_R, \блок_выхода_1_out_7 , \блок_выхода_1_rg_r_mux ;
  wire [15:0] outputA, outputB, \блок_вывода_1_out_8 ;
  wire [21:0] RG_SmsX2Size;

  D_Flip_Flop d_ff_1 (.clk(\input ), .D(P0), .Q(OperatingMode), .en(in_5[26]), .reset(in_5[0]));  // open: Qn, preset
  D_Flip_Flop d_ff_2 (.clk(\input ), .D(1'b1), .Q(ERROR), .en(in_5[19]), .reset(in_5[0]));  // open: Qn, preset
  \Сдвиговый_регистр_вправо  \u_сдвиговый_регистр_вправо_1  (
    .\input (in_3), .LOAD(in_5[25]), .clk(\input ), .RST(in_5[0]), .out_6(out_sign_A), .\output (output_A),
    .move(1'b0));
  \Сдвиговый_регистр_вправо  \u_сдвиговый_регистр_вправо_2  (
    .\input (in_3), .LOAD(in_5[24]), .clk(\input ), .RST(in_5[0]), .out_6(out_sign_B), .\output (output_B),
    .move(1'b0));
  nor nor_1 (P1, output_B[0], output_B[1], output_B[2], output_B[3], output_B[4], output_B[5], output_B[6]);
  \Блок_выхода  \u_блок_выхода_1  (
    .in_1(RG_E), .in_2(RG_R), .signB(QSB), .signA(QSA), .E(in_5[11]), .out_7(\блок_выхода_1_out_7 ),
    .RG_R_mux(\блок_выхода_1_rg_r_mux ));
  // Probe on output_A
  // Probe on output_B
  assign out_10 = not_1_out ? \блок_выхода_1_rg_r_mux  : 9'bz;  // Controlled_Buffer controlled_buffer_1
  assign out_11 = not_1_out ? \блок_выхода_1_out_7  : 9'bz;  // Controlled_Buffer controlled_buffer_2
  not not_1 (not_1_out, ERROR);
  \Подсчет_экспоненты  \u_подсчет_экспоненты_1  (
    .in_1(outputA), .in_2(outputB), .out_6(RG_Sexp), .clk(\input ), .rst(in_5[0]), .E(in_5[6]));
  MoveLeftRegister moveleftregister_1 (
    .load(in_5[10]), .move(1'b0), .clk(\input ), .rst(in_5[0]), .out(signA), .in_2(in_4), .out_7(outputA));
  MoveLeftRegister moveleftregister_2 (
    .load(in_5[9]), .move(1'b0), .clk(\input ), .rst(in_5[0]), .out(signB), .in_2(in_4), .out_7(outputB));
  Comparator #(.width(1), .mode("unsigned")) comparator_1 (.a(OMinput), .b(1'b1), .eq(P0));  // open: gt, lt
  D_Flip_Flop d_ff_3 (.clk(\input ), .D(out_sign_A), .Q(QSA), .en(in_5[23]), .reset(in_5[0]));  // open: Qn, preset
  D_Flip_Flop d_ff_4 (.clk(\input ), .D(out_sign_B), .Q(QSB), .en(in_5[22]), .reset(in_5[0]));  // open: Qn, preset
  \Запись_RG_R_и_RG_E  \u_запись_rg_r_и_rg_e_1  (
    .moveRG_R(in_5[15]), .ABS_B(ABS_B), .loadRG_R(in_5[16]), .moveRG_E(in_5[13]), .loadRG_E(in_5[14]),
    .outRG_E(RG_E), .outRG_R(RG_R), .inputRG_A(ABS_A), .loadRG_A(in_5[18]), .moveRG_A(in_5[17]),
    .rst(in_5[0]), .clk(\input ));
  // Probe on RG_R
  // Probe on RG_E
  \Проверка_введенных_чисел  \u_проверка_введенных_чисел_1  (.in_1(outputA), .in_2(outputB), .out(P3));
  D_Flip_Flop d_ff_5 (.clk(\input ), .D(P3), .Q(ERROR_2), .en(P3), .reset(in_5[0]));  // open: Qn, preset
  \Модуль_числа  \u_модуль_числа_1  (.in_1(output_A), .out_5(ABS_A), .in_3(\input ), .rst(in_5[0]), .clk(in_5[21]));
  \Модуль_числа  \u_модуль_числа_2  (.in_1(output_B), .out_5(ABS_B), .in_3(\input ), .rst(in_5[0]), .clk(in_5[20]));
  \Блок_умножения_мантисс  \u_блок_умножения_мантисс_1  (
    .load(in_5[5]), .RG_A(outputA), .clk(\input ), .rst(in_5[0]), .move(in_5[3]), .RG_B(outputB),
    .RG_SLoad(in_5[4]), .out_8(RG_SmsX2Size), .P1(P4));
  assign not_2_out = ~ABS_B;  // NOT_Gate not_2, 8 bits wide
  // Probe on ABS_A
  // Probe on ABS_B
  Adder adder_1 (.a(not_2_out), .b(8'h1), .out(NOT_B));  // open: cin, cout
  Counter #(.width(4), .max('h8), .ongoal("stay")) counter_1 (
    .count(in_5[12]), .Q(counter_1_q), .clk(\input ), .clr(in_5[0]));  // open: load, D, carry
  // Probe on NOT_B
  Comparator #(.width(4), .mode("unsigned")) comparator_2 (.a(counter_1_q), .b(4'b1000), .eq(P2));  // open: gt, lt
  xor xor_1 (xor_1_out, signA, signB);
  D_Flip_Flop d_ff_6 (.clk(\input ), .D(xor_1_out), .Q(signS), .en(in_5[7]), .reset(in_5[0]));  // open: Qn, preset
  \Блок_вывода  \u_блок_вывода_1  (
    .in_1(RG_SmsX2Size), .RG_SexpLoad(in_5[1]), .RG_Sexp(RG_Sexp), .RG_Ssign(signS), .clk(\input ),
    .rst(in_5[0]), .out_8(\блок_вывода_1_out_8 ), .RG_SmsLoad(in_5[2]));
  assign out_14 = not_3_out ? \блок_вывода_1_out_8  : 16'bz;  // Controlled_Buffer controlled_buffer_3
  not not_3 (not_3_out, ERROR_2);

  // Other names for the same wires on the sheet: clk = \input ; ERROR_prime = ERROR; ERROR_t = ERROR_2; rst = in_5[0];
  //   RG_SexpLoad = in_5[1]; RG_SmsLoad = in_5[2]; move = in_5[3]; RG_Sload = in_5[4]; loadAandB = in_5[5];
  //   SexpCalc = in_5[6]; signLoad = in_5[7]; ErrorLoad = in_5[8]; loadB = in_5[9]; loadA = in_5[10]; E = in_5[11];
  //   countLoad = in_5[12]; moveRG_E = in_5[13]; loadRG_E = in_5[14]; moveRG_R = in_5[15]; loadRG_R = in_5[16];
  //   moveRG_A = in_5[17]; loadRG_A = in_5[18]; errorLoad_t = in_5[19]; absBLoad = in_5[20]; absALoad = in_5[21];
  //   signBLoad = in_5[22]; signALoad = in_5[23]; load_B = in_5[24]; load_A = in_5[25]; OperatingModeLoad = in_5[26];
  //   input_prime[15:0] = in_4; input_t[7:0] = in_3

  // Notes on the sheet:
  //   Запись исходных данных в регистры
  //   Отлов ошибки деления на 0
  //   ERRORS UNIT
  //   Выходной блок
  //   числа 16-ти разрядные
  //   микро-команды для ОА
  //   RG_A
  //   RG_B
  //   Загрузка значений чисел EXP формата в регистры левого сдвига
  //   экспонент исходных чисел
  //   Признак перехода
  //   ПРИЗНАКИ
  //   loadA
  //   loadB
  //   ErrorLoad
  //   signLoad
  //   SexpCalc
  //   loadAandB
  //   RG_Sload
  //   move
  //   Подсчет конечной экспоненты операцией сложения двух
  //   RG_R result
  //   RG_E result
  //   RG_SmsLoad
  //   RG_SexpLoad
  //   rst
  //   RG_A
  //   RG_B
  //   Запоминание знаков исходных данных
  //   T_RA
  //   T_RB
  //   ПРИЗНАКИ
  //   OperatingModeLoad
  //   ПРИЗНАКИ
  //   load_A
  //   load_B
  //   signALoad
  //   signBLoad
  //   absALoad
  //   absBLoad
  //   errorLoad
  //   Цикл деления n раз
  //   loadRG_A
  //   moveRG_A
  //   loadRG_R
  //   moveRG_R
  //   loadRG_E
  //   moveRG_E
  //   countLoad
  //   E
  //   rst
  //   Блок проверки корректности введенных данных
  //   введенное число NaN будем считать ошибкой
  //   Вывод ошибки после прохождения условия
  //   (если найдены некорректные значения)
  //   Произведение операции умножения двух мантисс
  //   ОПИСАНИЕ МИКРО-КОМАНД ДЛЯ ОПЕРАЦИОННОГО АВТОМАТА
  //   Определение модуля исходных данных
  //   В ДОПОЛНИТЕЛЬНОМ КОДЕ
  //   Счетчик циклов
  //   НАЧАЛЬНОЕ СОСТОЯНИЕ + ВЫБОР РЕЖИМА РАБОТЫ АВТОМАТА
  //   ОПЕРАЦИОННЫЙ АВТОМАТ ВЫЧИСЛИТЕЛЬНОГО УСТРОЙСТВА,
  //   ВЫПОЛНЯЮЩЕГО ОПЕРАЦИЮ ДЕЛЕНИЯ ЧИСЕЛ, ЗАДАННЫХ
  //   Подсчет значения НеБ для выполнения операции деления
  //   ОПЕРАЦИОННЫЙ АВТОМАТ ВЫЧИСЛИТЕЛЬНОГО УСТРОЙСТВА,
  //   ВЫПОЛНЯЮЩЕГО ОПЕРАЦИЮ УМНОЖЕНИЯ ЧИСЕЛ, ЗАДАННЫХ В IEEE754
  //   Определение знака числа, полученного операцией умножения
  //   Признак перехода
  //   Организация ответа
endmodule
