// Logisim project Вычислительное Устройство_Операция Деления.circ as structural Verilog: 8 circuits, main circuit main
module main (
  input  [7:0] in_1,
  output [8:0] out_2,
  output [8:0] out_3
);

  wire ceo, clk, RI_out, rst, \оа_1_error , \оа_1_p0 , \оа_1_p1 ;
  wire [15:0] Y;

  Clock clock_1 (.out(clk));
  // Probe on out_2
  // Probe on in_1
  Button RI (.out(RI_out));
  Button button_1 (.out(rst));
  \ОА  \u_оа_1  (
    .\input (clk), .in_2(in_1), .in_3(Y), .P0(\оа_1_p0 ), .P1(\оа_1_p1 ), .ERROR(\оа_1_error ),
    .out_7(out_3), .out_8(out_2));
  filter filter_1 (.in_1(clk), .in_2(RI_out), .in_3(1'b1), .out_5(ceo));  // open: out_4
  // Probe on out_3
  LED led_1 (.in(\оа_1_error ));
  \УА  \u_уа_1  (.RI(ceo), .P0(\оа_1_p0 ), .P1(\оа_1_p1 ), .Ready_RST(rst), .clk(clk), .\микро_команды (Y));

  // Notes on the sheet:
  //   Значение частного
  //   Ready RST
  //   Значение остатка
endmodule

module \УА  (
  input  RI,
  input  P0,
  input  P1,
  input  Ready_RST,
  input  clk,
  output [15:0] \микро_команды 
);

  wire multiplexer_1_out;
  wire [1:0] rom_1_data_2;
  wire [3:0] multiplexer_2_out, register_1_q;
  wire [7:0] rom_1_data;

  Multiplexer #(.select(2), .disabled(0), .enable("false")) multiplexer_1 (
    .in0(RI), .in1(P0), .in2(P1), .in3(Ready_RST), .out(multiplexer_1_out), .sel(rom_1_data_2));
  Multiplexer #(.width(4), .disabled(0), .enable("false")) multiplexer_2 (
    .in0(rom_1_data[3:0]), .in1(rom_1_data[7:4]), .out(multiplexer_2_out), .sel(multiplexer_1_out));
  Register #(.width(4)) register_1 (.D(multiplexer_2_out), .Q(register_1_q), .clk(clk));  // open: en, clr
  ROM #(.addrWidth(4), .dataWidth(10)) rom_1 (.addr(register_1_q), .data({rom_1_data_2, rom_1_data}));  // open: sel
  ROM #(.addrWidth(4), .dataWidth(16)) rom_2 (.addr(register_1_q), .data(\микро_команды ));  // open: sel

  // Notes on the sheet:
  //   contents of rom_1 (hex, n*v repeats v):
  //   1d 2e 33 44 55 167 30f 88 99 aa bb 2c8 30f 1d 2e 30f
  //   contents of rom_2 (hex, n*v repeats v):
  //   1 8000 4000 3000 800 400 200 100 a0 8 40 4 2 0 0 2
  //   В ДОПОЛНИТЕЛЬНОМ КОДЕ
  //   УПРАВЛЯЮЩИЙ АВТОМАТ ВЫЧИСЛИТЕЛЬНОГО УСТРОЙСТВА,
  //   ВЫПОЛНЯЮЩЕГО ОПЕРАЦИЮ ДЕЛЕНИЯ ЧИСЕЛ, ЗАДАННЫХ
endmodule

module \ОА  (
  input  \input ,
  input  [7:0] in_2,
  input  [15:0] in_3,
  output P0,
  output P1,
  output ERROR,
  output [8:0] out_7,
  output [8:0] out_8
);

  wire out_sign_A, out_sign_B, QSA, QSB;
  wire [3:0] counter_1_q;
  wire [7:0] ABS_A, ABS_B, not_1_out, NOT_B, output_A, output_B;
  wire [8:0] RG_E, RG_R;

  D_Flip_Flop d_ff_1 (.clk(\input ), .D(1'b1), .Q(ERROR), .en(in_3[9]), .reset(in_3[0]));  // open: Qn, preset
  \Сдвиговый_регистр_вправо  \u_сдвиговый_регистр_вправо_1  (
    .\input (in_2), .LOAD(in_3[15]), .clk(\input ), .RST(in_3[0]), .out_6(out_sign_A), .\output (output_A),
    .move(1'b0));
  \Сдвиговый_регистр_вправо  \u_сдвиговый_регистр_вправо_2  (
    .\input (in_2), .LOAD(in_3[14]), .clk(\input ), .RST(in_3[0]), .out_6(out_sign_B), .\output (output_B),
    .move(1'b0));
  nor nor_1 (P0, output_B[0], output_B[1], output_B[2], output_B[3], output_B[4], output_B[5], output_B[6]);
  \Блок_выхода  \u_блок_выхода_1  (
    .in_1(RG_E), .in_2(RG_R), .signB(QSB), .signA(QSA), .E(in_3[1]), .out_7(out_8), .RG_R_mux(out_7));
  // Probe on output_A
  // Probe on output_B
  D_Flip_Flop d_ff_2 (.clk(\input ), .D(out_sign_A), .Q(QSA), .en(in_3[13]), .reset(in_3[0]));  // open: Qn, preset
  D_Flip_Flop d_ff_3 (.clk(\input ), .D(out_sign_B), .Q(QSB), .en(in_3[12]), .reset(in_3[0]));  // open: Qn, preset
  \Запись_RG_R_и_RG_E  \u_запись_rg_r_и_rg_e_1  (
    .moveRG_R(in_3[5]), .ABS_B(ABS_B), .loadRG_R(in_3[6]), .moveRG_E(in_3[3]), .loadRG_E(in_3[4]),
    .outRG_E(RG_E), .outRG_R(RG_R), .inputRG_A(ABS_A), .loadRG_A(in_3[8]), .moveRG_A(in_3[7]), .rst(in_3[0]),
    .clk(\input ));
  // Probe on RG_R
  // Probe on RG_E
  \Модуль_числа  \u_модуль_числа_1  (.in_1(output_A), .out_5(ABS_A), .in_3(\input ), .rst(in_3[0]), .clk(in_3[11]));
  \Модуль_числа  \u_модуль_числа_2  (.in_1(output_B), .out_5(ABS_B), .in_3(\input ), .rst(in_3[0]), .clk(in_3[10]));
  assign not_1_out = ~ABS_B;  // NOT_Gate not_1, 8 bits wide
  // Probe on ABS_A
  // Probe on ABS_B
  Adder adder_1 (.a(not_1_out), .b(8'h1), .out(NOT_B));  // open: cin, cout
  Counter #(.width(4), .max('h8), .ongoal("stay")) counter_1 (
    .count(in_3[2]), .Q(counter_1_q), .clk(\input ), .clr(in_3[0]));  // open: load, D, carry
  // Probe on NOT_B
  Comparator #(.width(4), .mode("unsigned")) comparator_1 (.a(counter_1_q), .b(4'b1000), .eq(P1));  // open: gt, lt

  // Other names for the same wires on the sheet: clk = \input ; rst = in_3[0]; E = in_3[1]; countLoad = in_3[2];
  //   moveRG_E = in_3[3]; loadRG_E = in_3[4]; moveRG_R = in_3[5]; loadRG_R = in_3[6]; moveRG_A = in_3[7];
  //   loadRG_A = in_3[8]; errorLoad = in_3[9]; absBLoad = in_3[10]; absALoad = in_3[11]; signBLoad = in_3[12];
  //   signALoad = in_3[13]; load_B = in_3[14]; load_A = in_3[15]; input_t[7:0] = in_2

  // Notes on the sheet:
  //   Запись исходных данных в регистры
  //   Отлов ошибки деления на 0
  //   ERRORS UNIT
  //   Выходной блок
  //   RG_A
  //   RG_B
  //   Признак перехода
  //   RG_R result
  //   RG_E result
  //   Запоминание знаков исходных данных
  //   T_RA
  //   T_RB
  //   ПРИЗНАКИ
  //   load_A
  //   load_B
  //   signALoad
  //   signBLoad
  //   absALoad
  //   absBLoad
  //   errorLoad
  //   Цикл деления n раз
  //   loadRG_A
  //   moveRG_A
  //   loadRG_R
  //   moveRG_R
  //   loadRG_E
  //   moveRG_E
  //   countLoad
  //   E
  //   rst
  //   тут проблема
  //   Определение модуля исходных данных
  //   В ДОПОЛНИТЕЛЬНОМ КОДЕ
  //   Счетчик циклов
  //   Загрузка микро-команд
  //   ОПЕРАЦИОННЫЙ АВТОМАТ ВЫЧИСЛИТЕЛЬНОГО УСТРОЙСТВА,
  //   ВЫПОЛНЯЮЩЕГО ОПЕРАЦИЮ ДЕЛЕНИЯ ЧИСЕЛ, ЗАДАННЫХ
  //   Подсчет значения НеБ для выполнения операции деления
  //   Признак перехода
endmodule

module \Сдвиговый_регистр_вправо  (
  input  [7:0] \input ,
  input  LOAD,
  input  clk,
  input  move,
  input  RST,
  output out_6,
  output [7:0] \output 
);

  wire multiplexer_1_out;

  Multiplexer #(.disabled(0), .enable("false")) multiplexer_1 (
    .in0(1'b0), .in1(1'b1), .out(multiplexer_1_out), .sel(LOAD));
  Shift_Register shift_register_1 (
    .shift(move), .in(1'b0), .clk(clk), .out(out_6), .load(multiplexer_1_out), .clr(RST), .d0(\input [0]),
    .q0(\output [0]), .d1(\input [1]), .q1(\output [1]), .d2(\input [2]), .q2(\output [2]), .d3(\input [3]),
    .q3(\output [3]), .d4(\input [4]), .q4(\output [4]), .d5(\input [5]), .q5(\output [5]), .d6(\input [6]),
    .q6(\output [6]), .d7(\input [7]), .q7(\output [7]));

  // Other names for the same wires on the sheet: _7 = \input [0]; _6 = \input [1]; _5 = \input [2]; _4 = \input [3];
  //   _3 = \input [4]; _2 = \input [5]; _1 = \input [6]; _0 = \input [7]
endmodule

module \Модуль_числа  (
  input  [7:0] in_1,
  input  clk,
  input  in_3,
  input  rst,
  output [7:0] out_5
);

  wire [7:0] adder_1_out, multiplexer_1_out, not_1_out;
  wire [7:7] register_1_q;

  assign not_1_out = ~in_1;  // NOT_Gate not_1, 8 bits wide
  Adder adder_1 (.a(not_1_out), .b(8'h1), .out(adder_1_out));  // open: cin, cout
  Multiplexer #(.width(8), .disabled(0), .enable("false")) multiplexer_1 (
    .in0(in_1), .in1(adder_1_out), .out(multiplexer_1_out), .sel(in_1[7]));
  Register #(.width(9)) register_1 (
    .D({1'b0, multiplexer_1_out}), .en(clk), .Q({out_5[7], register_1_q[7], out_5[6:0]}), .clk(in_3),
    .clr(rst));
  // Probe on {out_5[7], register_1_q[7], out_5[6:0]}

  // Notes on the sheet:
  //   input
  //   absLoad
  //   output
endmodule

module \Запись_RG_R_и_RG_E  (
  input  loadRG_A,
  input  [7:0] inputRG_A,
  input  loadRG_R,
  input  moveRG_R,
  input  moveRG_A,
  input  clk,
  input  rst,
  input  loadRG_E,
  input  moveRG_E,
  input  [7:0] ABS_B,
  output [8:0] outRG_R,
  output [8:0] outRG_E
);

  wire adder_2_cout, adder_3_cout, multiplexer_2_out, shift_register_1_out, shift_register_2_out;
  wire [8:0] adder_1_out, adder_2_out, adder_3_out, not_1_out, sign0, sign1;

  Shift_Register #(.length(9)) shift_register_1 (
    .shift(moveRG_A), .in(1'b0), .clk(clk), .out(shift_register_1_out), .load(loadRG_A), .clr(rst),
    .d0(inputRG_A[0]), .d1(inputRG_A[1]), .d2(inputRG_A[2]), .d3(inputRG_A[3]), .d4(inputRG_A[4]),
    .d5(inputRG_A[5]), .d6(inputRG_A[6]), .d7(inputRG_A[7]), .d8(1'b0));  // open: q0, q1, q2, q3, q4, q5, q6, q7, q8
  Shift_Register #(.length(9)) shift_register_2 (
    .shift(moveRG_R), .in(shift_register_1_out), .clk(clk), .out(shift_register_2_out), .load(loadRG_R),
    .clr(rst), .d0(sign1[0]), .q0(sign0[0]), .d1(sign1[1]), .q1(sign0[1]), .d2(sign1[2]), .q2(sign0[2]),
    .d3(sign1[3]), .q3(sign0[3]), .d4(sign1[4]), .q4(sign0[4]), .d5(sign1[5]), .q5(sign0[5]), .d6(sign1[6]),
    .q6(sign0[6]), .d7(sign1[7]), .q7(sign0[7]), .d8(sign1[8]), .q8(sign0[8]));
  assign not_1_out = ~{1'b0, ABS_B};  // NOT_Gate not_1, 9 bits wide
  Adder #(.width(9)) adder_1 (.a(not_1_out), .b(9'h1), .out(adder_1_out));  // open: cin, cout
  Adder #(.width(9)) adder_2 (.a(sign0), .b(adder_1_out), .out(adder_2_out), .cout(adder_2_cout));  // open: cin
  Adder #(.width(9)) adder_3 (.a(sign0), .b({1'b0, ABS_B}), .out(adder_3_out), .cout(adder_3_cout));  // open: cin
  Multiplexer #(.width(9), .disabled(0), .enable("false")) multiplexer_1 (
    .in0(adder_2_out), .in1(adder_3_out), .out(sign1), .sel(shift_register_2_out));
  Shift_Register #(.length(9)) shift_register_3 (
    .shift(moveRG_E), .in(multiplexer_2_out), .clk(clk), .load(loadRG_E), .clr(rst), .q0(outRG_E[0]),
    .q1(outRG_E[1]), .q2(outRG_E[2]), .q3(outRG_E[3]), .q4(outRG_E[4]), .q5(outRG_E[5]), .q6(outRG_E[6]),
    .q7(outRG_E[7]), .q8(outRG_E[8]));  // open: out, d0, d1, d2, d3, d4, d5, d6, d7, d8
  Multiplexer #(.disabled(0), .enable("false")) multiplexer_2 (
    .in0(adder_2_cout), .in1(adder_3_cout), .out(multiplexer_2_out), .sel(shift_register_2_out));
  Multiplexer #(.width(9), .disabled(0), .enable("false")) multiplexer_3 (
    .in0(sign0), .in1(sign1), .out(outRG_R), .sel(shift_register_2_out));

  // Notes on the sheet:
  //   RG_R
  //   RG_E
endmodule

module \Блок_выхода  (
  input  [8:0] in_1,
  input  [8:0] in_2,
  input  signB,
  input  signA,
  input  E,
  output [8:0] RG_R_mux,
  output [8:0] out_7
);

  wire [1:0] multiplexer_1_out;
  wire [8:0] not_1_out, not_2_out, NOT_RG_E____1, NOT_RG_R____1;

  assign not_1_out = ~in_1;  // NOT_Gate not_1, 9 bits wide
  assign not_2_out = ~in_2;  // NOT_Gate not_2, 9 bits wide
  Adder #(.width(9)) adder_1 (.a(not_1_out), .b(9'h1), .out(NOT_RG_E____1));  // open: cin, cout
  Adder #(.width(9)) adder_2 (.a(not_2_out), .b(9'h1), .out(NOT_RG_R____1));  // open: cin, cout
  Multiplexer #(.disabled(0)) multiplexer_1 (.in0(1'b0), .in1(1'b1), .out(multiplexer_1_out[0]), .sel(signB), .en(E));
  Multiplexer #(.disabled(0)) multiplexer_2 (.in0(1'b0), .in1(1'b1), .out(multiplexer_1_out[1]), .sel(signA), .en(E));
  Multiplexer #(.select(2), .width(9), .disabled(0)) multiplexer_3 (
    .in0(in_2), .in1(in_2), .in2(NOT_RG_R____1), .in3(NOT_RG_R____1), .out(RG_R_mux),
    .sel(multiplexer_1_out), .en(E));
  Multiplexer #(.select(2), .width(9), .disabled(0)) multiplexer_4 (
    .in0(in_1), .in1(NOT_RG_E____1), .in2(NOT_RG_E____1), .in3(in_1), .out(out_7), .sel(multiplexer_1_out),
    .en(E));

  // Other names for the same wires on the sheet: RG_E[8:0] = in_1; RG_R[8:0] = in_2

  // Notes on the sheet:
  //   RG_E
  //   RG_R
  //   RG_E mux
  //   resultRG_R
  //   resultRG_E
endmodule

module filter (
  input  in_1,
  input  in_2,
  input  in_3,
  output out_4,
  output out_5
);

  wire and_1_out, and_2_out, and_3_out, d_ff_1_q, d_ff_2_q, d_ff_3_q, xnor_1_out;
  wire [3:0] counter_1_q;

  Counter #(.width(4), .max('hf)) counter_1 (
    .count(in_3), .Q(counter_1_q), .clk(in_1), .clr(xnor_1_out));  // open: load, D, carry
  D_Flip_Flop d_ff_1 (.clk(in_1), .D(in_2), .Q(d_ff_1_q));  // open: Qn, preset, en, reset
  D_Flip_Flop d_ff_2 (.clk(in_1), .D(d_ff_1_q), .Q(d_ff_2_q));  // open: Qn, preset, en, reset
  and and_1 (and_1_out, counter_1_q[0], counter_1_q[1], counter_1_q[2], counter_1_q[3]);
  and and_2 (and_2_out, and_1_out, in_3);
  D_Flip_Flop d_ff_3 (.clk(in_1), .D(d_ff_2_q), .Q(d_ff_3_q), .en(and_2_out));  // open: Qn, preset, reset
  and and_3 (and_3_out, d_ff_2_q, and_2_out);
  buf buffer_1 (out_4, d_ff_3_q);
  xnor xnor_1 (xnor_1_out, d_ff_3_q, d_ff_2_q);
  D_Flip_Flop d_ff_4 (.clk(in_1), .D(and_3_out), .Q(out_5));  // open: Qn, preset, en, reset

  // Other names for the same wires on the sheet: CLK = in_1
endmodule
