// Logisim project Вычислительное Устройство_Операция Умножения IEEE754.circ as structural Verilog: 10 circuits, main circuit main
module main (
  input  [15:0] in_1,
  output [15:0] out_2
);

  wire button_1_out, clk, RI, RI_out, \оа_1_error , \оа_1_p0 , \оа_1_p1 ;
  wire [10:0] \уа_1_out_6 ;

  Clock clock_1 (.out(clk));
  Button u_RI (.out(RI_out));
  Button button_1 (.out(button_1_out));
  \ОА  \u_оа_1  (
    .in_1(clk), .in_2(in_1), .in_3(\уа_1_out_6 ), .P0(\оа_1_p0 ), .ERROR(\оа_1_error ), .P1(\оа_1_p1 ),
    .out_6(out_2));
  filter filter_1 (.in_1(clk), .in_2(RI_out), .in_3(1'b1), .out_5(RI));  // open: out_4
  LED led_1 (.in(\оа_1_error ));
  \УА  \u_уа_1  (.RI(RI), .P0(\оа_1_p0 ), .P1(\оа_1_p1 ), .ReadyRST(button_1_out), .clk(clk), .out_6(\уа_1_out_6 ));

  // Notes on the sheet:
  //   Ready RST
  //   Ввод чисел
  //   Результат выполнения умножения чисел, представленных в IEEE754
endmodule

module \ОА  (
  input  in_1,
  input  [15:0] in_2,
  input  [10:0] in_3,
  output P0,
  output ERROR,
  output [15:0] out_6,
  output P1
);

  wire not_1_out, signA, signB, signS, xor_1_out;
  wire [6:0] RG_Sexp;
  wire [15:0] outputA, outputB, \блок_вывода_1_out_8 ;
  wire [21:0] RG_SmsX2Size;

  \Подсчет_экспоненты  \u_подсчет_экспоненты_1  (
    .in_1(outputA), .in_2(outputB), .out_6(RG_Sexp), .clk(in_1), .rst(in_3[0]), .E(in_3[6]));
  MoveLeftRegister moveleftregister_1 (
    .load(in_3[10]), .move(1'b0), .clk(in_1), .rst(in_3[0]), .out(signA), .in_2(in_2), .out_7(outputA));
  MoveLeftRegister moveleftregister_2 (
    .load(in_3[9]), .move(1'b0), .clk(in_1), .rst(in_3[0]), .out(signB), .in_2(in_2), .out_7(outputB));
  \Проверка_введенных_чисел  \u_проверка_введенных_чисел_1  (.in_1(outputA), .in_2(outputB), .out(P0));
  D_Flip_Flop d_ff_1 (.clk(in_1), .D(P0), .Q(ERROR), .en(P0), .reset(in_3[0]));  // open: Qn, preset
  \Блок_умножения_мантисс  \u_блок_умножения_мантисс_1  (
    .load(in_3[5]), .RG_A(outputA), .clk(in_1), .rst(in_3[0]), .move(in_3[3]), .RG_B(outputB),
    .RG_SLoad(in_3[4]), .out_8(RG_SmsX2Size), .P1(P1));
  D_Flip_Flop d_ff_2 (.clk(in_1), .D(xor_1_out), .Q(signS), .en(in_3[7]));  // open: Qn, preset, reset
  xor xor_1 (xor_1_out, signA, signB);
  \Блок_вывода  \u_блок_вывода_1  (
    .in_1(RG_SmsX2Size), .RG_SexpLoad(in_3[1]), .RG_Sexp(RG_Sexp), .RG_Ssign(signS), .clk(in_1),
    .rst(in_3[0]), .out_8(\блок_вывода_1_out_8 ), .RG_SmsLoad(in_3[2]));
  assign out_6 = not_1_out ? \блок_вывода_1_out_8  : 16'bz;  // Controlled_Buffer controlled_buffer_1
  not not_1 (not_1_out, ERROR);

  // Other names for the same wires on the sheet: clk = in_1; rst = in_3[0]; RG_SexpLoad = in_3[1];
  //   RG_SmsLoad = in_3[2]; move = in_3[3]; RG_Sload = in_3[4]; loadAandB = in_3[5]; SexpCalc = in_3[6];
  //   signLoad = in_3[7]; ErrorLoad = in_3[8]; loadB = in_3[9]; loadA = in_3[10]; input[15:0] = in_2

  // Notes on the sheet:
  //   числа 16-ти разрядные
  //   экспонент исходных чисел
  //   микро-команды для ОА
  //   Загрузка значений чисел EXP формата в регистры левого сдвига
  //   Подсчет конечной экспоненты операцией сложения двух
  //   loadA
  //   loadB
  //   ErrorLoad
  //   signLoad
  //   SexpCalc
  //   loadAandB
  //   RG_Sload
  //   move
  //   RG_A
  //   RG_B
  //   ПРИЗНАКИ
  //   RG_SmsLoad
  //   RG_SexpLoad
  //   rst
  //   Блок проверки корректности введенных данных
  //   введенное число NaN будем считать ошибкой
  //   Вывод ошибки после прохождения условия
  //   (если найдены некорректные значения)
  //   Произведение операции умножения двух мантисс
  //   Определение знака числа, полученного операцией умножения
  //   Организация ответа
endmodule

module MoveRightRegister (
  input  load,
  input  [15:0] in_2,
  input  move,
  input  clk,
  input  rst,
  output out,
  output [15:0] out_7
);

  Shift_Register #(.length(16)) shift_register_1 (
    .shift(move), .in(1'b0), .clk(clk), .out(out), .load(load), .clr(rst), .d0(in_2[15]), .q0(out_7[15]),
    .d1(in_2[14]), .q1(out_7[14]), .d2(in_2[13]), .q2(out_7[13]), .d3(in_2[12]), .q3(out_7[12]),
    .d4(in_2[11]), .q4(out_7[11]), .d5(in_2[10]), .q5(out_7[10]), .d6(in_2[9]), .q6(out_7[9]), .d7(in_2[8]),
    .q7(out_7[8]), .d8(in_2[7]), .q8(out_7[7]), .d9(in_2[6]), .q9(out_7[6]), .d10(in_2[5]), .q10(out_7[5]),
    .d11(in_2[4]), .q11(out_7[4]), .d12(in_2[3]), .q12(out_7[3]), .d13(in_2[2]), .q13(out_7[2]),
    .d14(in_2[1]), .q14(out_7[1]), .d15(in_2[0]), .q15(out_7[0]));

  // Notes on the sheet:
  //   input
  //   output
endmodule

module MoveLeftRegister (
  input  load,
  input  [15:0] in_2,
  input  move,
  input  clk,
  input  rst,
  output out,
  output [15:0] out_7
);

  Shift_Register #(.length(16)) shift_register_1 (
    .shift(move), .in(1'b0), .clk(clk), .out(out), .load(load), .clr(rst), .d0(in_2[0]), .q0(out_7[0]),
    .d1(in_2[1]), .q1(out_7[1]), .d2(in_2[2]), .q2(out_7[2]), .d3(in_2[3]), .q3(out_7[3]), .d4(in_2[4]),
    .q4(out_7[4]), .d5(in_2[5]), .q5(out_7[5]), .d6(in_2[6]), .q6(out_7[6]), .d7(in_2[7]), .q7(out_7[7]),
    .d8(in_2[8]), .q8(out_7[8]), .d9(in_2[9]), .q9(out_7[9]), .d10(in_2[10]), .q10(out_7[10]),
    .d11(in_2[11]), .q11(out_7[11]), .d12(in_2[12]), .q12(out_7[12]), .d13(in_2[13]), .q13(out_7[13]),
    .d14(in_2[14]), .q14(out_7[14]), .d15(in_2[15]), .q15(out_7[15]));

  // Notes on the sheet:
  //   input
  //   output
endmodule

module \Проверка_введенных_чисел  (
  input  [15:0] in_1,
  input  [15:0] in_2,
  output out
);

  wire _1, _2, _3, _4, _5, and_4_out, and_5_out, and_6_out, and_7_out, comparator_1_eq, comparator_2_eq,
       comparator_3_eq, comparator_4_eq, comparator_5_eq, comparator_6_eq, comparator_7_eq, comparator_8_eq,
       nor_1_out, nor_2_out, nor_3_out, nor_4_out, or_2_out, or_3_out;

  or or_1 (out, _1, _2, _5, _3, _4);
  or or_2 (or_2_out, in_1[0], in_1[1], in_1[2], in_1[3], in_1[4], in_1[5], in_1[6], in_1[7], in_1[8], in_1[9]);
  or or_3 (or_3_out, in_2[0], in_2[1], in_2[2], in_2[3], in_2[4], in_2[5], in_2[6], in_2[7], in_2[8], in_2[9]);
  nor nor_1 (nor_1_out, in_1[10], in_1[11], in_1[12], in_1[13], in_1[14], in_1[0], in_1[1], in_1[2], in_1[3], in_1[4], in_1[5], in_1[6], in_1[7], in_1[8], in_1[9]);
  Comparator #(.width(5), .mode("unsigned")) comparator_1 (
    .a(in_1[14:10]), .b({5{1'b1}}), .eq(comparator_1_eq));  // open: gt, lt
  and and_1 (_1, comparator_1_eq, or_2_out);
  Comparator #(.width(5), .mode("unsigned")) comparator_2 (
    .a(in_2[14:10]), .b({5{1'b1}}), .eq(comparator_2_eq));  // open: gt, lt
  and and_2 (_2, comparator_2_eq, or_3_out);
  Comparator #(.width(5), .mode("unsigned")) comparator_3 (
    .a(in_2[14:10]), .b({5{1'b1}}), .eq(comparator_3_eq));  // open: gt, lt
  nor nor_2 (nor_2_out, in_2[0], in_2[1], in_2[2], in_2[3], in_2[4], in_2[5], in_2[6], in_2[7], in_2[8], in_2[9]);
  and and_3 (_4, nor_1_out, and_4_out);
  and and_4 (and_4_out, comparator_3_eq, nor_2_out);
  nor nor_3 (nor_3_out, in_2[10], in_2[11], in_2[12], in_2[13], in_2[14], in_2[0], in_2[1], in_2[2], in_2[3], in_2[4], in_2[5], in_2[6], in_2[7], in_2[8], in_2[9]);
  Comparator #(.width(5), .mode("unsigned")) comparator_4 (
    .a(in_1[14:10]), .b({5{1'b1}}), .eq(comparator_4_eq));  // open: gt, lt
  nor nor_4 (nor_4_out, in_1[0], in_1[1], in_1[2], in_1[3], in_1[4], in_1[5], in_1[6], in_1[7], in_1[8], in_1[9]);
  Comparator #(.width(10), .mode("unsigned")) comparator_5 (
    .a(in_1[9:0]), .b({10{1'b0}}), .eq(comparator_5_eq));  // open: gt, lt
  Comparator #(.width(5), .mode("unsigned")) comparator_6 (
    .a(in_1[14:10]), .b({5{1'b1}}), .eq(comparator_6_eq));  // open: gt, lt
  Comparator #(.width(10), .mode("unsigned")) comparator_7 (
    .a(in_2[9:0]), .b({10{1'b0}}), .eq(comparator_7_eq));  // open: gt, lt
  Comparator #(.width(5), .mode("unsigned")) comparator_8 (
    .a(in_2[14:10]), .b({5{1'b1}}), .eq(comparator_8_eq));  // open: gt, lt
  and and_5 (and_5_out, comparator_4_eq, nor_4_out);
  and and_6 (and_6_out, comparator_5_eq, comparator_6_eq);
  and and_7 (and_7_out, comparator_7_eq, comparator_8_eq);
  and and_8 (_3, nor_3_out, and_5_out);
  or or_4 (_5, and_6_out, and_7_out);

  // Other names for the same wires on the sheet: expA[4:0] = in_1[14:10]; inputA[15:0] = in_1;
  //   mantissA[9:0] = in_1[9:0]; expB[4:0] = in_2[14:10]; inputB[15:0] = in_2; mantissB[9:0] = in_2[9:0]

  // Notes on the sheet:
  //   inputA
  //   inputB
endmodule

module \Подсчет_экспоненты  (
  input  [15:0] in_1,
  input  [15:0] in_2,
  input  E,
  input  clk,
  input  rst,
  output [6:0] out_6
);

  wire adder_3_cout, comparator_1_eq, comparator_2_eq, nor_1_out, nor_2_out, not_2_out, or_1_out, or_2_out;
  wire [4:0] adder_1_out;
  wire [5:0] adder_2_out, adder_4_out, adder_5_out, adder_6_out, expResult, multiplexer_1_out,
       multiplexer_2_out, not_1_out;
  wire [5:5] adder_1_cout;

  Adder #(.width(5)) adder_1 (
    .a(in_1[14:10]), .b(in_2[14:10]), .out(adder_1_out), .cout(adder_1_cout[5]));  // open: cin
  assign not_1_out = ~6'b001111;  // NOT_Gate not_1, 6 bits wide
  Adder #(.width(6)) adder_2 (.a(not_1_out), .b(6'b000001), .out(adder_2_out));  // open: cin, cout
  Adder #(.width(6)) adder_3 (
    .a({adder_1_cout[5], adder_1_out}), .b(adder_2_out), .out(expResult), .cout(adder_3_cout));  // open: cin
  Comparator #(.width(6)) comparator_1 (.a(expResult), .b({6{1'b1}}), .eq(comparator_1_eq));  // open: gt, lt
  or or_1 (or_1_out, comparator_1_eq, adder_3_cout);
  nor nor_1 (nor_1_out, in_2[10], in_2[11], in_2[12], in_2[13], in_2[14]);
  nor nor_2 (nor_2_out, in_1[10], in_1[11], in_1[12], in_1[13], in_1[14]);
  Adder #(.width(6)) adder_4 (.a(expResult), .b(6'b000001), .out(adder_4_out));  // open: cin, cout
  Adder #(.width(6)) adder_5 (.a(expResult), .b(6'b000010), .out(adder_5_out));  // open: cin, cout
  Adder #(.width(6)) adder_6 (.a(expResult), .b(6'b000011), .out(adder_6_out));  // open: cin, cout
  or or_2 (or_2_out, nor_1_out, nor_2_out);
  Multiplexer #(.width(6), .disabled(0), .enable("false")) multiplexer_1 (
    .in0(multiplexer_2_out), .in1(adder_4_out), .out(multiplexer_1_out), .sel(comparator_1_eq));
  Multiplexer #(.width(6), .disabled(0), .enable("false")) multiplexer_2 (
    .in0(adder_5_out), .in1(adder_6_out), .out(multiplexer_2_out), .sel(or_2_out));
  Comparator #(.width(6), .mode("unsigned")) comparator_2 (
    .a(multiplexer_1_out), .b({6{1'b0}}), .eq(comparator_2_eq));  // open: gt, lt
  Register #(.width(6)) register_1 (.D(multiplexer_1_out), .en(1'b1), .Q(out_6[5:0]), .clk(clk), .clr(rst));
  Multiplexer #(.disabled(0), .enable("false")) multiplexer_3 (
    .in0(not_2_out), .in1(1'b0), .out(out_6[6]), .sel(comparator_2_eq));
  // Probe on out_6
  not not_2 (not_2_out, or_1_out);

  // Other names for the same wires on the sheet: expA[4:0] = in_1[14:10]; expB[4:0] = in_2[14:10]; sign = out_6[6]

  // Notes on the sheet:
  //   inA
  //   inB
  //   outSexp
endmodule

module \Блок_умножения_мантисс  (
  input  [15:0] RG_A,
  input  [15:0] RG_B,
  input  load,
  input  clk,
  input  rst,
  input  move,
  input  RG_SLoad,
  output [21:0] out_8,
  output P1
);

  wire adder_1_cout, comparator_1_lt, d_ff_1_q, not_1_out, RG_BlastElem, RG_Sms1_out;
  wire [3:0] counter_1_q;
  wire [10:0] adder_1_out, multiplexer_1_out, RG_Ams, RG_B_t;
  wire [10:10] or_1_out, or_2_out;

  Shift_Register #(.length(11)) RG_Sms1 (
    .shift(move), .in(d_ff_1_q), .clk(clk), .out(RG_Sms1_out), .load(RG_SLoad), .clr(rst),
    .d0(multiplexer_1_out[10]), .q0(out_8[21]), .d1(multiplexer_1_out[9]), .q1(out_8[20]),
    .d2(multiplexer_1_out[8]), .q2(out_8[19]), .d3(multiplexer_1_out[7]), .q3(out_8[18]),
    .d4(multiplexer_1_out[6]), .q4(out_8[17]), .d5(multiplexer_1_out[5]), .q5(out_8[16]),
    .d6(multiplexer_1_out[4]), .q6(out_8[15]), .d7(multiplexer_1_out[3]), .q7(out_8[14]),
    .d8(multiplexer_1_out[2]), .q8(out_8[13]), .d9(multiplexer_1_out[1]), .q9(out_8[12]),
    .d10(multiplexer_1_out[0]), .q10(out_8[11]));
  or or_1 (or_1_out[10], RG_A[10], RG_A[11], RG_A[12], RG_A[13], RG_A[14]);
  or or_2 (or_2_out[10], RG_B[10], RG_B[11], RG_B[12], RG_B[13], RG_B[14]);
  Shift_Register #(.length(11)) RG_Sms2 (
    .shift(move), .in(RG_Sms1_out), .clk(clk), .load(1'b0), .clr(rst), .q0(out_8[10]), .q1(out_8[9]),
    .q2(out_8[8]), .q3(out_8[7]), .q4(out_8[6]), .q5(out_8[5]), .q6(out_8[4]), .q7(out_8[3]), .q8(out_8[2]),
    .q9(out_8[1]), .q10(out_8[0]));  // open: out, d0, d1, d2, d3, d4, d5, d6, d7, d8, d9, d10
  Register #(.width(11)) register_1 (.D({or_1_out[10], RG_A[9:0]}), .en(load), .Q(RG_Ams), .clk(clk), .clr(rst));
  Shift_Register #(.length(11)) u_RG_B (
    .shift(move), .in(1'b0), .clk(clk), .out(RG_BlastElem), .load(load), .clr(rst), .d0(or_2_out[10]),
    .q0(RG_B_t[10]), .d1(RG_B[9]), .q1(RG_B_t[9]), .d2(RG_B[8]), .q2(RG_B_t[8]), .d3(RG_B[7]),
    .q3(RG_B_t[7]), .d4(RG_B[6]), .q4(RG_B_t[6]), .d5(RG_B[5]), .q5(RG_B_t[5]), .d6(RG_B[4]), .q6(RG_B_t[4]),
    .d7(RG_B[3]), .q7(RG_B_t[3]), .d8(RG_B[2]), .q8(RG_B_t[2]), .d9(RG_B[1]), .q9(RG_B_t[1]), .d10(RG_B[0]),
    .q10(RG_B_t[0]));
  Counter #(.width(4), .max('hb), .ongoal("stay")) counter_1 (
    .count(comparator_1_lt), .Q(counter_1_q), .clk(move), .clr(rst));  // open: load, D, carry
  Comparator #(.width(4), .mode("unsigned")) comparator_1 (
    .a(counter_1_q), .b(4'b1011), .eq(P1), .lt(comparator_1_lt));  // open: gt
  Adder #(.width(11)) adder_1 (.a(RG_Ams), .b(out_8[21:11]), .out(adder_1_out), .cout(adder_1_cout));  // open: cin
  D_Flip_Flop d_ff_1 (.clk(clk), .D(adder_1_cout), .Q(d_ff_1_q), .reset(not_1_out));  // open: Qn, preset, en
  not not_1 (not_1_out, RG_BlastElem);
  Multiplexer #(.width(11), .disabled(0), .enable("false")) multiplexer_1 (
    .in0(out_8[21:11]), .in1(adder_1_out), .out(multiplexer_1_out), .sel(RG_BlastElem));

  // Other names for the same wires on the sheet: _0_9_prime[9:0] = RG_B[9:0]; _0_9[9:0] = RG_A[9:0]; loadAandB = load;
  //   RG_SmsMoved[10:0] = out_8[10:0]; RG_Sms[10:0] = out_8[21:11]

  // Notes on the sheet:
  //   output X2 ms
  //   RG_A
endmodule

module \Блок_вывода  (
  input  [21:0] in_1,
  input  RG_SexpLoad,
  input  [6:0] RG_Sexp,
  input  RG_SmsLoad,
  input  RG_Ssign,
  input  clk,
  input  rst,
  output [15:0] out_8
);

  wire and_1_out, and_2_out, comparator_1_gt, comparator_1_lt, comparator_2_gt, d_ff_1_q, multiplexer_1_out,
       not_1_out, not_2_out, or_1_out, shift_register_1_out, shift_register_1_q11;
  wire [0:0] adder_1_cout;
  wire [6:0] adder_2_out, multiplexer_2_out, RG_Sexp_minus_minus;
  wire [6:5] multiplexer_3_out;
  wire [9:0] adder_1_out, multiplexer_4_out, shift_register_1_q12;

  Comparator #(.width(7)) comparator_1 (
    .a(RG_Sexp_minus_minus), .b({7{1'b0}}), .gt(comparator_1_gt), .lt(comparator_1_lt));  // open: eq
  Multiplexer #(.disabled(0), .enable("false")) multiplexer_1 (
    .in0(and_1_out), .in1(1'b1), .out(multiplexer_1_out), .sel(RG_SexpLoad));
  and and_1 (and_1_out, comparator_1_gt, not_1_out);
  Shift_Register #(.length(22)) shift_register_1 (
    .shift(and_1_out), .in(1'b0), .clk(clk), .out(shift_register_1_out), .load(RG_SmsLoad), .clr(rst),
    .d0(in_1[0]), .d1(in_1[1]), .d2(in_1[2]), .d3(in_1[3]), .d4(in_1[4]), .d5(in_1[5]), .d6(in_1[6]),
    .d7(in_1[7]), .d8(in_1[8]), .d9(in_1[9]), .d10(in_1[10]), .d11(in_1[11]), .q11(shift_register_1_q11),
    .d12(in_1[12]), .q12(shift_register_1_q12[0]), .d13(in_1[13]), .q13(shift_register_1_q12[1]),
    .d14(in_1[14]), .q14(shift_register_1_q12[2]), .d15(in_1[15]), .q15(shift_register_1_q12[3]),
    .d16(in_1[16]), .q16(shift_register_1_q12[4]), .d17(in_1[17]), .q17(shift_register_1_q12[5]),
    .d18(in_1[18]), .q18(shift_register_1_q12[6]), .d19(in_1[19]), .q19(shift_register_1_q12[7]),
    .d20(in_1[20]), .q20(shift_register_1_q12[8]), .d21(in_1[21]), .q21(shift_register_1_q12[9]));  // open: q0, q1, q2, q3, q4, q5, q6, q7, q8, q9, q10
  Multiplexer #(.width(7), .disabled(0), .enable("false")) multiplexer_2 (
    .in0(adder_2_out), .in1({7{1'b0}}), .out(multiplexer_2_out), .sel(comparator_1_lt));
  Counter #(.width(7), .max('h7f), .ongoal("load")) counter_1 (
    .load(multiplexer_1_out), .D(RG_Sexp), .count(and_1_out), .Q(RG_Sexp_minus_minus), .clk(clk), .clr(rst));  // open: carry
  Adder #(.width(10)) adder_1 (
    .a(shift_register_1_q12), .b(10'h1), .out(adder_1_out), .cout(adder_1_cout[0]));  // open: cin
  Multiplexer #(.width(7), .disabled(0), .enable("false")) multiplexer_3 (
    .in0(multiplexer_2_out), .in1(7'b0011111), .out({multiplexer_3_out, out_8[14:10]}), .sel(comparator_2_gt));
  Comparator #(.width(7)) comparator_2 (.a(multiplexer_2_out), .b(7'b0011111), .gt(comparator_2_gt));  // open: eq, lt
  Multiplexer #(.width(10), .disabled(0), .enable("false")) multiplexer_4 (
    .in0(shift_register_1_q12), .in1(adder_1_out), .out(multiplexer_4_out), .sel(shift_register_1_q11));
  Adder #(.width(7)) adder_2 (
    .a({{6{1'b0}}, adder_1_cout[0]}), .b(RG_Sexp_minus_minus), .out(adder_2_out));  // open: cin, cout
  or or_1 (or_1_out, comparator_2_gt, comparator_1_lt);
  Multiplexer #(.width(10), .disabled(0), .enable("false")) multiplexer_5 (
    .in0(multiplexer_4_out), .in1({10{1'b0}}), .out(out_8[9:0]), .sel(or_1_out));
  D_Flip_Flop d_ff_1 (
    .clk(clk), .D(shift_register_1_out), .Q(d_ff_1_q), .en(and_2_out), .reset(rst));  // open: Qn, preset
  not not_1 (not_1_out, d_ff_1_q);
  not not_2 (not_2_out, RG_SmsLoad);
  and and_2 (and_2_out, not_2_out, not_1_out);

  assign out_8[15] = RG_Ssign;

  // Other names for the same wires on the sheet: RG_SexpRes[4:0] = out_8[14:10]; RG_SmsRes[9:0] = out_8[9:0];
  //   RG_Sms[21:0] = in_1

  // Notes on the sheet:
  //   RG_Sms
  //   result
  //   move
  //   знак после запятой
endmodule

module \УА  (
  input  RI,
  input  P0,
  input  P1,
  input  ReadyRST,
  input  clk,
  output [10:0] out_6
);

  wire multiplexer_1_out;
  wire [1:0] rom_1_data_3;
  wire [3:0] multiplexer_2_out, register_1_q, rom_1_data, rom_1_data_2;

  Multiplexer #(.select(2), .disabled(0), .enable("false")) multiplexer_1 (
    .in0(RI), .in1(P0), .in2(P1), .in3(ReadyRST), .out(multiplexer_1_out), .sel(rom_1_data_3));
  Multiplexer #(.width(4), .disabled(0), .enable("false")) multiplexer_2 (
    .in0(rom_1_data), .in1(rom_1_data_2), .out(multiplexer_2_out), .sel(multiplexer_1_out));
  Register #(.width(4)) register_1 (.D(multiplexer_2_out), .Q(register_1_q), .clk(clk));  // open: en, clr
  ROM #(.addrWidth(4), .dataWidth(10)) rom_1 (
    .addr(register_1_q), .data({rom_1_data_3, rom_1_data_2, rom_1_data}));  // open: sel
  ROM #(.addrWidth(4), .dataWidth(11)) rom_2 (.addr(register_1_q), .data(out_6));  // open: sel
  // Probe on rom_1_data
  // Probe on rom_1_data_2
  // Probe on rom_1_data_3

  // Notes on the sheet:
  //   contents of rom_1 (hex, n*v repeats v):
  //   1b 2c 134 30d 55 66 77 88 297 aa 30d 1b 2c 30d
  //   contents of rom_2 (hex, n*v repeats v):
  //   1 400 200 100 80 40 20 10 8 6
endmodule

module filter (
  input  in_1,
  input  in_2,
  input  in_3,
  output out_4,
  output out_5
);

  wire and_1_out, and_2_out, and_3_out, d_ff_1_q, d_ff_2_q, d_ff_3_q, xnor_1_out;
  wire [3:0] counter_1_q;

  Counter #(.width(4), .max('hf)) counter_1 (
    .count(in_3), .Q(counter_1_q), .clk(in_1), .clr(xnor_1_out));  // open: load, D, carry
  D_Flip_Flop d_ff_1 (.clk(in_1), .D(in_2), .Q(d_ff_1_q));  // open: Qn, preset, en, reset
  D_Flip_Flop d_ff_2 (.clk(in_1), .D(d_ff_1_q), .Q(d_ff_2_q));  // open: Qn, preset, en, reset
  and and_1 (and_1_out, counter_1_q[0], counter_1_q[1], counter_1_q[2], counter_1_q[3]);
  and and_2 (and_2_out, and_1_out, in_3);
  D_Flip_Flop d_ff_3 (.clk(in_1), .D(d_ff_2_q), .Q(d_ff_3_q), .en(and_2_out));  // open: Qn, preset, reset
  and and_3 (and_3_out, d_ff_2_q, and_2_out);
  buf buffer_1 (out_4, d_ff_3_q);
  xnor xnor_1 (xnor_1_out, d_ff_3_q, d_ff_2_q);
  D_Flip_Flop d_ff_4 (.clk(in_1), .D(and_3_out), .Q(out_5));  // open: Qn, preset, en, reset

  // Other names for the same wires on the sheet: CLK = in_1
endmodule
